// Logisim project АВС_ЛР4.circ as structural Verilog: 1 circuit, main circuit 4
module _4 (
  input  in_1,
  input  in_2,
  input  in_3,
  input  in_4,
  input  in_5,
  input  in_6,
  input  in_7,
  input  in_8,
  input  in_9,
  input  in_10,
  input  in_11,
  input  in_12,
  input  in_13,
  output out_14,
  output out_15,
  output out_16,
  output out_17,
  output out_18,
  output out_19,
  output out_20,
  output out_21,
  output out_22,
  output out_23,
  output out_24,
  output out_25
);

  wire nand_1_out, nand_2_out, nand_3_out, nand_4_out, nand_10_out, nand_11_out, nand_12_out, nand_13_out,
       nand_17_out, nand_18_out;

  nor nor_1 (out_14, in_1, out_16);
  nor nor_2 (out_16, out_14, in_3);
  nand nand_1 (nand_1_out, in_5, in_7);
  nand nand_2 (nand_2_out, in_7, in_8);
  nand nand_3 (nand_3_out, in_10, nand_4_out);
  nand nand_4 (nand_4_out, in_12, in_12);
  nand nand_5 (out_18, nand_1_out, out_20);
  nand nand_6 (out_20, out_18, nand_2_out);
  nand nand_7 (out_22, nand_3_out, out_24);
  nand nand_8 (out_24, out_22, nand_4_out);
  nand nand_9 (out_15, in_2, out_17);
  nand nand_10 (nand_10_out, in_6, in_6);
  nand nand_11 (nand_11_out, nand_10_out, in_9);
  nand nand_12 (nand_12_out, in_11, in_11);
  nand nand_13 (nand_13_out, in_13, in_13);
  nand nand_14 (out_17, out_15, in_4);
  nand nand_15 (out_19, nand_10_out, out_21);
  nand nand_16 (out_21, out_19, nand_11_out);
  nand nand_17 (nand_17_out, in_11, nand_13_out);
  nand nand_18 (nand_18_out, nand_12_out, in_13);
  nand nand_19 (out_23, nand_17_out, out_25);
  nand nand_20 (out_25, out_23, nand_18_out);

  // Notes on the sheet:
  //   Синхронный RS-триггер
  //   R-триггер
  //   Асинхронный RS-триггер с прямыми входами (2 элемента ИЛИ-НЕ)
  //   S-триггер
  //   E-триггер
  //   Асинхронный RS-триггер с инверсными входами (2 элемента И-НЕ)
endmodule
