// Logisim project АВС ЛР5.circ as structural Verilog: 1 circuit, main circuit main
module main (
  input  in_1,
  input  D,
  input  C,
  input  J,
  input  K,
  output Q,
  output Q_2,
  output out_8,
  output nQ,
  output nQ_2,
  output out_11
);

  wire _3_out, _4_out, C_out, clock_1_out, nand_1_out, nand_2_out, nand_5_out, nand_6_out, nand_7_out,
       nand_8_out, not_1_out, not_2_out, not_3_out, not_4_out;

  Clock clock_1 (.out(clock_1_out));
  not not_1 (not_1_out, in_1);
  not not_2 (not_2_out, clock_1_out);
  nand nand_1 (nand_1_out, not_1_out, in_1, clock_1_out, nand_2_out);
  nand nand_2 (nand_2_out, nand_1_out, clock_1_out);
  nand nand_3 (nQ_2, nand_1_out, not_2_out, nQ_2);
  nand nand_4 (nQ_2, nQ_2, nand_2_out, not_2_out);
  Clock u_C (.out(C_out));
  not not_3 (not_3_out, C_out);
  not not_4 (not_4_out, C_out);
  nand nand_5 (nand_5_out, D, nand_6_out);
  nand nand_6 (nand_6_out, nand_5_out, not_3_out, C_out);
  nand nand_7 (nand_7_out, D, nand_8_out);
  nand nand_8 (nand_8_out, nand_7_out, C_out, not_4_out);
  nand nand_9 (out_8, nand_6_out, out_11);
  nand nand_10 (out_11, out_8, nand_8_out);
  nand _1 (Q, _3_out, nQ);
  nand _2 (nQ, Q, _4_out, C);
  nand _3 (_3_out, Q, J);
  nand _4 (_4_out, nQ, K);

  assign Q_2 = nQ_2;

  // Notes on the sheet:
  //   D триггер
  //   T триггер
  //   JK триггер
endmodule
