// Logisim project АВС_3.1.circ as structural Verilog: 1 circuit, main circuit 1
module _1 (
  input  a,
  input  b,
  input  c,
  input  d,
  input  e,
  output out_6
);

  wire and_1_out, and_2_out, and_3_out, and_4_out, and_5_out, not_1_out, not_2_out, not_3_out, not_4_out,
       not_5_out, not_6_out, not_7_out, not_8_out, not_9_out, not_10_out, not_11_out, not_12_out, not_13_out;

  not not_1 (not_1_out, a);
  not not_2 (not_2_out, b);
  not not_3 (not_3_out, c);
  not not_4 (not_4_out, d);
  not not_5 (not_5_out, a);
  not not_6 (not_6_out, b);
  not not_7 (not_7_out, d);
  not not_8 (not_8_out, a);
  not not_9 (not_9_out, c);
  not not_10 (not_10_out, d);
  not not_11 (not_11_out, a);
  not not_12 (not_12_out, b);
  not not_13 (not_13_out, d);
  and and_1 (and_1_out, not_1_out, not_2_out, not_3_out, not_4_out, e);
  and and_2 (and_2_out, not_5_out, not_6_out, c, not_7_out, e);
  and and_3 (and_3_out, not_8_out, b, not_9_out, not_10_out, e);
  and and_4 (and_4_out, not_11_out, b, c, d, e);
  and and_5 (and_5_out, a, not_12_out, c, not_13_out, e);
  nor nor_1 (out_6, and_1_out, and_2_out, and_3_out, and_4_out, and_5_out);

  // Notes on the sheet:
  //   1 Вариант
endmodule
