// Logisim project АВС_3.2.circ as structural Verilog: 1 circuit, main circuit main
module main (
  input  a,
  input  b,
  input  c,
  input  d,
  input  e,
  output x,
  output y,
  output z
);

  wire nand_1_out, nand_2_out, nand_3_out, nand_4_out, nand_5_out, nand_6_out, nand_7_out, nand_8_out,
       nand_9_out;

  nand nand_1 (nand_1_out, a, a);
  nand nand_2 (nand_2_out, a, a);
  nand nand_3 (nand_3_out, a, a);
  nand nand_4 (nand_4_out, c, c);
  nand nand_5 (nand_5_out, a, a);
  nand nand_6 (nand_6_out, nand_1_out, c);
  nand nand_7 (nand_7_out, nand_2_out, b);
  nand nand_8 (nand_8_out, nand_3_out, nand_4_out, d);
  nand nand_9 (nand_9_out, nand_5_out, b);
  nand nand_10 (y, nand_6_out, nand_7_out);
  nand nand_11 (z, nand_8_out, nand_9_out);

  assign x = a;
endmodule
